# Fritzing sketch montage avec résistance (saved by Fritzing 0.9.2b)
breadboards: 1

parts:
  LED1 = LED - 5mm [color="Red (633nm)" package="5 mm [THT]"]
  part = Arduino Uno (Rev3)
  R1 = Resistor [tolerance=±5% resistance=150 package=THT]

nets:
  N1: LED1.cathode, part.GND
  N2: LED1.anode, R1.Pin_0
  N3: part.D8, R1.Pin_1
