# Fritzing sketch Fiche n°1 (saved by Fritzing 0.9.2b)
breadboards: 1

parts:
  Composant1 = Arduino Uno (Rev3)
  LED1 = LED - 5mm [color="Red (633nm)" package="5 mm [THT]"]

nets:
  N1: Composant1.D13/SCK, LED1.anode
  N2: Composant1.GND, LED1.cathode
