# Fritzing sketch Fiche n°2 (saved by Fritzing 0.9.2b)
circuit board: 4.28967cm x 2.04292cm
breadboards: 1

parts:
  R1 = Resistor [tolerance=±5% resistance=150 package=THT]
  LED1 = LED - 5mm [color="Red (633nm)" package="5 mm [THT]"]
  S1 = Pushbutton [package="[THT]"]
  R2 = Resistor [tolerance=±5% resistance=10k package=THT]
  Composant1 = Arduino Uno (Rev3)

nets:
  N1: R1.Pin_0, Composant1.D9_PWM
  N2: R1.Pin_1, LED1.anode
  N3: LED1.cathode, R2.Pin_1, Composant1.GND
  N4: S1.Pin_1, S1.Pin_2, R2.Pin_0, Composant1.D8
  N5: S1.Pin_3, S1.Pin_4, Composant1.5V

notes:
  LED avec résistance en série
  Bouton-poussoir avec résistance pull-down

// code stored in the sketch: Fichen.ino
/*   ----------------  Fiche n°2  ----------------------
      Une led pilotée par un interrupteur 
*/


const int Led = 8;     // LED en broche 8
const int Bouton = 9;  // le bouton en borche 9
int BoutonEtat;  // variable pour enregistrer l'état du bouton
 
// the setup routine runs once when you press reset:
void setup() {
  // initialize the digital pin as an output.
  pinMode(Led, OUTPUT);   // Broche de la led en tant que sortie 
  pinMode(Bouton, INPUT); // Broche du bouton poussoir en tant d'entrée
}

// the loop routine runs over and over again forever:
void loop() {
  BoutonEtat = digitalRead(Bouton);
  if (BoutonEtat == HIGH) {
  	digitalWrite(Led, HIGH);   // Allume la LED
  }
  else {
  	digitalWrite(Led, LOW);    // éteint la LED  
  }
}
